// Logisim project sqrt2.circ as structural Verilog: 34 circuits, main circuit main
module main (
  input  ENABLE,
  input  [15:0] IO_DATA_IN,
  output NAN,
  output PINF,
  output NINF,
  output RESULT,
  output [15:0] IO_DATA_OUT
);

  wire CLK_out;

  Clock CLK (.out(CLK_out));
  sqrt sqrt_1 (
    .CLK(CLK_out), .ENABLE(ENABLE), .IO_DATA_IN(IO_DATA_IN), .IS_NAN(NAN), .IS_PINF(PINF), .IS_NINF(NINF),
    .RESULT(RESULT), .IO_DATA_OUT(IO_DATA_OUT));
endmodule

module sqrt (
  input  CLK,
  input  ENABLE,
  input  [15:0] IO_DATA_IN,
  output IS_NAN,
  output IS_PINF,
  output IS_NINF,
  output RESULT,
  output [15:0] IO_DATA_OUT
);

  wire algorithm_1_enddd, and_1_out, and_2_out, and_5_out, and_6_out, beg_1_greater, beg_1_nq,
       deconstruct_1_sign, detecting_1_nan, detecting_1_negzero, detecting_1_pinf, nand_1_out, or_1_out,
       transmission_1_p2, transmission_1_p3, transmission_2_p2;
  wire [4:0] correcting_1_realexp, deconstruct_1_exp;
  wire [9:0] algorithm_1_ans;
  wire [11:0] correcting_1_man, deconstruct_1_mantis, num12_1_num;
  wire [15:0] construct_1_ans, nan_1_correctnan_mbnothing, num16_1_num, pinf_1_outpt, transmission_1_p4,
       transmission_2_p4, zero_1_zero16;

  // Transmission_Gate #(.width(16)) transmission_1: pin names not known; wires that end beside it: IO_DATA_IN, transmission_1_p2, transmission_1_p3, transmission_1_p4
  not not_1 (transmission_1_p3, transmission_1_p2);
  num16 num16_1 (.inp(transmission_1_p4), .ReadWrite(beg_1_nq), .Enable(ENABLE), .num(num16_1_num));
  deconstruct deconstruct_1 (
    .inp(num16_1_num), .mantis(deconstruct_1_mantis), .exp(deconstruct_1_exp), .sign(deconstruct_1_sign));
  beg beg_1 (.CLK(CLK), .ENABLE(ENABLE), .NQ(beg_1_nq), .equal(transmission_1_p2), .greater(beg_1_greater));
  // Transmission_Gate #(.width(16)) transmission_2: pin names not known; wires that end beside it: IO_DATA_IN, transmission_2_p2, beg_1_greater, transmission_2_p4
  not not_2 (transmission_2_p2, beg_1_greater);
  correcting correcting_1 (
    .mantis(deconstruct_1_mantis), .exp(deconstruct_1_exp), .realexp(correcting_1_realexp),
    .man(correcting_1_man));
  detecting detecting_1 (
    .sign(deconstruct_1_sign), .mantis(deconstruct_1_mantis), .exp(deconstruct_1_exp),
    .negzero(detecting_1_negzero), .PINF(detecting_1_pinf), .NAN(detecting_1_nan));
  or or_1 (or_1_out, detecting_1_negzero, detecting_1_pinf, detecting_1_nan);
  and and_1 (and_1_out, beg_1_greater, ENABLE);
  and and_2 (and_2_out, detecting_1_negzero, and_1_out);
  num12 num12_1 (.inp({{7{1'b0}}, correcting_1_realexp}), .ReadWrite(beg_1_nq), .Enable(ENABLE), .num(num12_1_num));
  and and_3 (IS_PINF, detecting_1_pinf, and_1_out);
  and and_4 (IS_NAN, detecting_1_nan, and_1_out);
  zero zero_1 (.detnegzero(and_2_out), .zero16(zero_1_zero16));
  and and_5 (and_5_out, ENABLE, beg_1_greater);
  NaN nan_1 (
    .detnan(IS_NAN), .sign(deconstruct_1_sign), .exp(deconstruct_1_exp), .mantis(deconstruct_1_mantis),
    .correctNaN_mbnothing(nan_1_correctnan_mbnothing));
  pinf pinf_1 (.detpinf(IS_PINF), .outpt(pinf_1_outpt));
  and and_6 (and_6_out, and_5_out, or_1_out);
  nand nand_1 (nand_1_out, ENABLE, beg_1_greater);
  assign transmission_2_p4 = zero_1_zero16 | pinf_1_outpt | nan_1_correctnan_mbnothing | construct_1_ans;  // OR_Gate or_2, 16 bits wide
  algorithm algorithm_1 (
    .CLK(CLK), .Enable(ENABLE), .is_first_iter(nand_1_out), .mantis(correcting_1_man),
    .is_answered(and_6_out), .enddd(algorithm_1_enddd), .ans(algorithm_1_ans));
  or or_3 (RESULT, and_6_out, algorithm_1_enddd);
  construct construct_1 (.mantis(algorithm_1_ans), .exp(num12_1_num[4:0]), .ans(construct_1_ans));

  assign IO_DATA_OUT = IO_DATA_IN;
  assign IS_NINF = 1'b0;
endmodule

module algorithm (
  input  CLK,
  input  Enable,
  input  is_first_iter,
  input  [11:0] mantis,
  input  is_answered,
  output enddd,
  output [9:0] ans
);

  wire and_5_out, and_7_out, and_8_out, compc_1_equal, compc_1_greater, nor_1_out, not_1_out, not_2_out,
       not_3_out, not_4_out, not_5_out, not_6_out, not_7_out, not_8_out, or_2_out, or_4_out;
  wire [0:0] or_6_out;
  wire [1:0] num24_3_num_2;
  wire [11:0] and_1_out, and_4_out, l12_1_outp, num12_1_num, num12_2_num, or_1_out, to12_1_bit12,
       to12_2_bit12;
  wire [23:0] and_2_out, and_3_out, and_9_out, and_10_out, and_11_out, bits24difc_1_dif24bit,
       bits24summator_1_sum24bit, bits24summator_2_sum24bit, bits24summator_3_sum24bit, l24_1_outp,
       l24_2_outp, l24_3_outp, l24_4_outp, l24_5_outp, l24_6_outp, num24_1_num, num24_2_num, num24_3_num,
       num24_4_num, num24_5_num, num24_6_num, or_3_out, to24_1_bit24, to24_2_bit24, to24_3_bit24,
       to24_4_bit24, to24_5_bit24;
  wire [23:10] and_6_out;

  To12 to12_1 (.\bit (is_first_iter), .bit12(to12_1_bit12));
  L24 l24_1 (.inp({num24_3_num[23:12], num24_3_num_2, num24_3_num[9:0]}), .outp(l24_1_outp));
  assign and_1_out = 12'h1 & to12_1_bit12;  // AND_Gate and_1, 12 bits wide
  not not_1 (not_1_out, is_first_iter);
  assign or_1_out = and_1_out | and_4_out;  // OR_Gate or_1, 12 bits wide
  L24 l24_2 (.inp(l24_1_outp), .outp(l24_2_outp));
  not not_2 (not_2_out, CLK);
  To24 to24_1 (.\bit (is_first_iter), .bit24(to24_1_bit24));
  or or_2 (or_2_out, mantis[0], mantis[1], mantis[2], mantis[3], mantis[4], mantis[5], mantis[6], mantis[7], mantis[8], mantis[9], mantis[10], mantis[11]);
  To12 to12_2 (.\bit (not_1_out), .bit12(to12_2_bit12));
  not not_3 (not_3_out, or_2_out);
  assign and_2_out = to24_1_bit24 & {{12{1'b0}}, mantis};  // AND_Gate and_2, 24 bits wide
  num24 num24_1 (.inp(l24_2_outp), .ReadWrite(not_2_out), .Enable(Enable), .num(num24_1_num));
  To24 to24_2 (.\bit (not_1_out), .bit24(to24_2_bit24));
  assign and_3_out = num24_1_num & to24_2_bit24;  // AND_Gate and_3, 24 bits wide
  num12 num12_1 (.inp(or_1_out), .ReadWrite(nor_1_out), .Enable(Enable), .num(num12_1_num));
  assign or_3_out = and_3_out | and_2_out;  // OR_Gate or_3, 24 bits wide
  L12 l12_1 (.inp(num12_1_num), .outp(l12_1_outp));
  num12 num12_2 (.inp(l12_1_outp), .ReadWrite(and_7_out), .Enable(Enable), .num(num12_2_num));
  assign and_4_out = to12_2_bit12 & num12_2_num;  // AND_Gate and_4, 12 bits wide
  and and_5 (and_5_out, not_3_out, or_1_out[1]);
  or or_4 (or_4_out, is_answered, is_first_iter);
  not not_4 (not_4_out, or_4_out);
  num24 num24_2 (.inp(and_11_out), .ReadWrite(CLK), .Enable(Enable), .num(num24_2_num));
  To24 to24_3 (.\bit (not_4_out), .bit24(to24_3_bit24));
  assign {and_6_out, ans} = num24_2_num & to24_3_bit24;  // AND_Gate and_6, 24 bits wide
  or or_5 (enddd, and_5_out, or_1_out[11], is_answered);
  L24 l24_3 (.inp(num24_2_num), .outp(l24_3_outp));
  not not_5 (not_5_out, enddd);
  nor nor_1 (nor_1_out, CLK, enddd);
  and and_7 (and_7_out, CLK, not_5_out);
  L24 l24_4 (.inp(l24_3_outp), .outp(l24_4_outp));
  not not_6 (not_6_out, CLK);
  not not_7 (not_7_out, enddd);
  and and_8 (and_8_out, not_6_out, not_7_out);
  BITS24SUMMATOR bits24summator_1 (
    .first(l24_4_outp), .second(24'h1), .sum24bit(bits24summator_1_sum24bit));  // open: remain
  CompC compc_1 (
    .first(bits24summator_3_sum24bit), .second(bits24summator_1_sum24bit), .equal(compc_1_equal),
    .greater(compc_1_greater));  // open: less
  or or_6 (or_6_out[0], compc_1_equal, compc_1_greater);
  not not_8 (not_8_out, is_first_iter);
  To24 to24_4 (.\bit (or_6_out[0]), .bit24(to24_4_bit24));
  assign and_9_out = to24_4_bit24 & bits24summator_1_sum24bit;  // AND_Gate and_9, 24 bits wide
  To24 to24_5 (.\bit (not_8_out), .bit24(to24_5_bit24));
  BITS24SUMMATOR bits24summator_2 (
    .first(l24_3_outp), .second({{23{1'b0}}, or_6_out[0]}), .sum24bit(bits24summator_2_sum24bit));  // open: remain
  BITS24DifC bits24difc_1 (
    .first(bits24summator_3_sum24bit), .second(and_9_out), .dif24bit(bits24difc_1_dif24bit));  // open: remain
  num24 num24_3 (
    .inp(or_3_out), .ReadWrite(CLK), .Enable(Enable),
    .num({num24_3_num[23:12], num24_3_num_2, num24_3_num[9:0]}));
  num24 num24_4 (.inp(bits24summator_2_sum24bit), .ReadWrite(and_8_out), .Enable(Enable), .num(num24_4_num));
  num24 num24_5 (.inp(bits24difc_1_dif24bit), .ReadWrite(and_8_out), .Enable(Enable), .num(num24_5_num));
  assign and_10_out = to24_5_bit24 & num24_5_num;  // AND_Gate and_10, 24 bits wide
  assign and_11_out = to24_5_bit24 & num24_4_num;  // AND_Gate and_11, 24 bits wide
  num24 num24_6 (.inp(and_10_out), .ReadWrite(CLK), .Enable(Enable), .num(num24_6_num));
  L24 l24_5 (.inp(num24_6_num), .outp(l24_5_outp));
  L24 l24_6 (.inp(l24_5_outp), .outp(l24_6_outp));
  BITS24SUMMATOR bits24summator_3 (
    .first({{22{1'b0}}, num24_3_num_2}), .second(l24_6_outp), .sum24bit(bits24summator_3_sum24bit));  // open: remain
endmodule

module deconstruct (
  input  [15:0] inp,
  output [11:0] mantis,
  output [4:0] exp,
  output sign
);


  assign exp = inp[14:10];
  assign mantis = {2'b00, inp[9:0]};
  assign sign = inp[15];
endmodule

module construct (
  input  [9:0] mantis,
  input  [4:0] exp,
  output [15:0] ans
);


  assign ans = {1'b0, exp, mantis};
endmodule

module detectexp (
  input  [4:0] exp,
  output [4:0] correct_exp,
  output is_even
);

  wire [4:0] and_1_out, and_2_out, not_2_out;
  wire [11:0] bits12difc_1_dif12bit;

  not not_1 (is_even, exp[0]);
  assign and_1_out = exp & {5{exp[0]}};  // AND_Gate and_1, 5 bits wide
  assign not_2_out = ~{5{exp[0]}};  // NOT_Gate not_2, 5 bits wide
  BITS12DifC bits12difc_1 (
    .first({{7{1'b0}}, exp}), .second(12'h1), .dif12bit(bits12difc_1_dif12bit));  // open: prevC, remain
  assign and_2_out = not_2_out & bits12difc_1_dif12bit[4:0];  // AND_Gate and_2, 5 bits wide
  assign correct_exp = and_1_out | and_2_out;  // OR_Gate or_1, 5 bits wide
endmodule

module R12 (
  input  [11:0] inp,
  output [11:0] outp
);


  assign outp = {1'b0, inp[11:1]};
endmodule

module L12 (
  input  [11:0] inp,
  output [11:0] outp
);


  assign outp = {inp[10:0], 1'b0};
endmodule

module L24 (
  input  [23:0] inp,
  output [23:0] outp
);


  assign outp = {inp[22:0], 1'b0};
endmodule

module To12 (
  input  \bit ,
  output [11:0] bit12
);


  assign bit12 = {12{\bit }};
endmodule

module To16 (
  input  \bit ,
  output [15:0] bit16
);


  assign bit16 = {16{\bit }};
endmodule

module To24 (
  input  \bit ,
  output [23:0] bit24
);


  assign bit24 = {24{\bit }};
endmodule

module shiftman (
  input  [11:0] mantis,
  input  [11:0] shift,
  output [11:0] tmp_result,
  output [11:0] tmp_shift
);

  wire not_1_out;
  wire [11:0] and_1_out, and_2_out, and_3_out, l12_1_outp, not_2_out, to12_1_bit12;

  not not_1 (not_1_out, mantis[9]);
  L12 l12_1 (.inp(mantis), .outp(l12_1_outp));
  To12 to12_1 (.\bit (not_1_out), .bit12(to12_1_bit12));
  assign and_1_out = l12_1_outp & to12_1_bit12;  // AND_Gate and_1, 12 bits wide
  assign and_2_out = to12_1_bit12 & 12'h1;  // AND_Gate and_2, 12 bits wide
  assign not_2_out = ~to12_1_bit12;  // NOT_Gate not_2, 12 bits wide
  assign and_3_out = mantis & not_2_out;  // AND_Gate and_3, 12 bits wide
  assign tmp_result = and_3_out | and_1_out;  // OR_Gate or_1, 12 bits wide
  BITS12SUMMATOR bits12summator_1 (.first(shift), .second(and_2_out), .sum12bit(tmp_shift));  // open: prevC, remain
endmodule

module normedmantis (
  input  [11:0] mantis,
  output [11:0] normedman,
  output [11:0] shift
);

  wire [11:0] shiftman_1_tmp_result, shiftman_1_tmp_shift, shiftman_2_tmp_result, shiftman_2_tmp_shift,
       shiftman_3_tmp_result, shiftman_3_tmp_shift, shiftman_4_tmp_result, shiftman_4_tmp_shift,
       shiftman_5_tmp_result, shiftman_5_tmp_shift, shiftman_6_tmp_result, shiftman_6_tmp_shift,
       shiftman_7_tmp_result, shiftman_7_tmp_shift, shiftman_8_tmp_result, shiftman_8_tmp_shift,
       shiftman_9_tmp_result, shiftman_9_tmp_shift, shiftman_10_tmp_result, shiftman_10_tmp_shift;
  wire [11:10] l12_1_outp;

  shiftman shiftman_1 (
    .mantis(mantis), .shift({12{1'b0}}), .tmp_result(shiftman_1_tmp_result), .tmp_shift(shiftman_1_tmp_shift));
  shiftman shiftman_2 (
    .mantis(shiftman_1_tmp_result), .shift(shiftman_1_tmp_shift), .tmp_result(shiftman_2_tmp_result),
    .tmp_shift(shiftman_2_tmp_shift));
  shiftman shiftman_3 (
    .mantis(shiftman_2_tmp_result), .shift(shiftman_2_tmp_shift), .tmp_result(shiftman_3_tmp_result),
    .tmp_shift(shiftman_3_tmp_shift));
  shiftman shiftman_4 (
    .mantis(shiftman_3_tmp_result), .shift(shiftman_3_tmp_shift), .tmp_result(shiftman_4_tmp_result),
    .tmp_shift(shiftman_4_tmp_shift));
  shiftman shiftman_5 (
    .mantis(shiftman_4_tmp_result), .shift(shiftman_4_tmp_shift), .tmp_result(shiftman_5_tmp_result),
    .tmp_shift(shiftman_5_tmp_shift));
  shiftman shiftman_6 (
    .mantis(shiftman_5_tmp_result), .shift(shiftman_5_tmp_shift), .tmp_result(shiftman_6_tmp_result),
    .tmp_shift(shiftman_6_tmp_shift));
  shiftman shiftman_7 (
    .mantis(shiftman_6_tmp_result), .shift(shiftman_6_tmp_shift), .tmp_result(shiftman_7_tmp_result),
    .tmp_shift(shiftman_7_tmp_shift));
  shiftman shiftman_8 (
    .mantis(shiftman_7_tmp_result), .shift(shiftman_7_tmp_shift), .tmp_result(shiftman_8_tmp_result),
    .tmp_shift(shiftman_8_tmp_shift));
  shiftman shiftman_9 (
    .mantis(shiftman_8_tmp_result), .shift(shiftman_8_tmp_shift), .tmp_result(shiftman_9_tmp_result),
    .tmp_shift(shiftman_9_tmp_shift));
  shiftman shiftman_10 (
    .mantis(shiftman_9_tmp_result), .shift(shiftman_9_tmp_shift), .tmp_result(shiftman_10_tmp_result),
    .tmp_shift(shiftman_10_tmp_shift));
  L12 l12_1 (.inp(shiftman_10_tmp_result), .outp({l12_1_outp, normedman[9:0]}));
  BITS12SUMMATOR bits12summator_1 (
    .first(shiftman_10_tmp_shift), .second(12'h1), .sum12bit(shift));  // open: prevC, remain

  assign normedman[11:10] = 2'b01;
endmodule

module SUMMATOR (
  input  first,
  input  second,
  input  previous,
  output remain,
  output current
);

  wire and_1_out, and_2_out, xor_1_out, xor_2_out;

  xor xor_1 (xor_1_out, first, second);
  and and_1 (and_1_out, first, second);
  and and_2 (and_2_out, xor_1_out, previous);
  or or_1 (remain, and_2_out, and_1_out);
  xor xor_2 (xor_2_out, second, first);
  xor xor_3 (current, xor_2_out, previous);
endmodule

module BITS24DifC (
  input  [23:0] first,
  input  [23:0] second,
  output [23:0] dif24bit,
  output remain
);

  wire bits12difc_1_remain;

  BITS12DifC bits12difc_1 (
    .first(first[11:0]), .prevC(1'b0), .second(second[11:0]), .dif12bit(dif24bit[11:0]),
    .remain(bits12difc_1_remain));
  BITS12DifC bits12difc_2 (
    .first(first[23:12]), .prevC(bits12difc_1_remain), .second(second[23:12]), .dif12bit(dif24bit[23:12]),
    .remain(remain));
endmodule

module CompC (
  input  [23:0] first,
  input  [23:0] second,
  output equal,
  output greater,
  output less
);

  wire not_1_out, or_1_out;
  wire [23:0] bits24difc_1_dif24bit;

  BITS24DifC bits24difc_1 (.first(first), .second(second), .dif24bit(bits24difc_1_dif24bit), .remain(less));
  or or_1 (or_1_out, bits24difc_1_dif24bit[0], bits24difc_1_dif24bit[1], bits24difc_1_dif24bit[2], bits24difc_1_dif24bit[3], bits24difc_1_dif24bit[4], bits24difc_1_dif24bit[5], bits24difc_1_dif24bit[6], bits24difc_1_dif24bit[7], bits24difc_1_dif24bit[8], bits24difc_1_dif24bit[9], bits24difc_1_dif24bit[10], bits24difc_1_dif24bit[11], bits24difc_1_dif24bit[13], bits24difc_1_dif24bit[14], bits24difc_1_dif24bit[15], bits24difc_1_dif24bit[16], bits24difc_1_dif24bit[17], bits24difc_1_dif24bit[18], bits24difc_1_dif24bit[19], bits24difc_1_dif24bit[20], bits24difc_1_dif24bit[21], bits24difc_1_dif24bit[22], bits24difc_1_dif24bit[23]);
  not not_1 (not_1_out, less);
  not not_2 (equal, or_1_out);
  and and_1 (greater, or_1_out, not_1_out);
endmodule

module BITS12DifC (
  input  [11:0] first,
  input  prevC,
  input  [11:0] second,
  output [11:0] dif12bit,
  output remain
);

  wire diffc_1_r, diffc_2_r, diffc_3_r, diffc_4_r, diffc_5_r, diffc_6_r, diffc_7_r, diffc_8_r, diffc_9_r,
       diffc_10_r, diffc_11_r;

  DiffC diffc_1 (.first(first[0]), .second(second[0]), .prev(prevC), .R(diffc_1_r), .Dif(dif12bit[0]));
  DiffC diffc_2 (.first(first[1]), .second(second[1]), .prev(diffc_1_r), .R(diffc_2_r), .Dif(dif12bit[1]));
  DiffC diffc_3 (.first(first[2]), .second(second[2]), .prev(diffc_2_r), .R(diffc_3_r), .Dif(dif12bit[2]));
  DiffC diffc_4 (.first(first[3]), .second(second[3]), .prev(diffc_3_r), .R(diffc_4_r), .Dif(dif12bit[3]));
  DiffC diffc_5 (.first(first[4]), .second(second[4]), .prev(diffc_4_r), .R(diffc_5_r), .Dif(dif12bit[4]));
  DiffC diffc_6 (.first(first[5]), .second(second[5]), .prev(diffc_5_r), .R(diffc_6_r), .Dif(dif12bit[5]));
  DiffC diffc_7 (.first(first[6]), .second(second[6]), .prev(diffc_6_r), .R(diffc_7_r), .Dif(dif12bit[6]));
  DiffC diffc_8 (.first(first[7]), .second(second[7]), .prev(diffc_7_r), .R(diffc_8_r), .Dif(dif12bit[7]));
  DiffC diffc_9 (.first(first[8]), .second(second[8]), .prev(diffc_8_r), .R(diffc_9_r), .Dif(dif12bit[8]));
  DiffC diffc_10 (.first(first[9]), .second(second[9]), .prev(diffc_9_r), .R(diffc_10_r), .Dif(dif12bit[9]));
  DiffC diffc_11 (.first(first[10]), .second(second[10]), .prev(diffc_10_r), .R(diffc_11_r), .Dif(dif12bit[10]));
  DiffC diffc_12 (.first(first[11]), .second(second[11]), .prev(diffc_11_r), .R(remain), .Dif(dif12bit[11]));
endmodule

module DiffC (
  input  first,
  input  second,
  input  prev,
  output R,
  output Dif
);

  wire and_1_out, and_2_out, not_1_out, not_2_out, xor_1_out;

  xor xor_1 (xor_1_out, first, second);
  not not_1 (not_1_out, first);
  and and_1 (and_1_out, not_1_out, second);
  not not_2 (not_2_out, xor_1_out);
  xor xor_2 (Dif, xor_1_out, prev);
  and and_2 (and_2_out, not_2_out, prev);
  or or_1 (R, and_1_out, and_2_out);
endmodule

module D_Triggers (
  input  CLK,
  input  Data,
  input  Enable,
  output Q,
  output NQ
);

  wire and_1_out, and_2_out, nor_2_out, not_1_out, not_2_out, or_1_out, por_1_out;

  not not_1 (not_1_out, Data);
  POR por_1 (.out(por_1_out));
  and and_1 (and_1_out, CLK, Data);
  and and_2 (and_2_out, not_1_out, CLK);
  not not_2 (not_2_out, Enable);
  or or_1 (or_1_out, not_2_out, por_1_out);
  nor nor_1 (Q, and_2_out, NQ);
  nor nor_2 (nor_2_out, Q, and_1_out);
  or or_2 (NQ, nor_2_out, or_1_out);
endmodule

module BITS12SUMMATOR (
  input  [11:0] first,
  input  prevC,
  input  [11:0] second,
  output [11:0] sum12bit,
  output remain
);

  wire summator_1_remain, summator_2_remain, summator_3_remain, summator_4_remain, summator_5_remain,
       summator_6_remain, summator_7_remain, summator_8_remain, summator_9_remain, summator_10_remain,
       summator_11_remain;

  SUMMATOR summator_1 (
    .first(first[0]), .second(second[0]), .previous(prevC), .remain(summator_1_remain), .current(sum12bit[0]));
  SUMMATOR summator_2 (
    .first(first[1]), .second(second[1]), .previous(summator_1_remain), .remain(summator_2_remain),
    .current(sum12bit[1]));
  SUMMATOR summator_3 (
    .first(first[2]), .second(second[2]), .previous(summator_2_remain), .remain(summator_3_remain),
    .current(sum12bit[2]));
  SUMMATOR summator_4 (
    .first(first[3]), .second(second[3]), .previous(summator_3_remain), .remain(summator_4_remain),
    .current(sum12bit[3]));
  SUMMATOR summator_5 (
    .first(first[4]), .second(second[4]), .previous(summator_4_remain), .remain(summator_5_remain),
    .current(sum12bit[4]));
  SUMMATOR summator_6 (
    .first(first[5]), .second(second[5]), .previous(summator_5_remain), .remain(summator_6_remain),
    .current(sum12bit[5]));
  SUMMATOR summator_7 (
    .first(first[6]), .second(second[6]), .previous(summator_6_remain), .remain(summator_7_remain),
    .current(sum12bit[6]));
  SUMMATOR summator_8 (
    .first(first[7]), .second(second[7]), .previous(summator_7_remain), .remain(summator_8_remain),
    .current(sum12bit[7]));
  SUMMATOR summator_9 (
    .first(first[8]), .second(second[8]), .previous(summator_8_remain), .remain(summator_9_remain),
    .current(sum12bit[8]));
  SUMMATOR summator_10 (
    .first(first[9]), .second(second[9]), .previous(summator_9_remain), .remain(summator_10_remain),
    .current(sum12bit[9]));
  SUMMATOR summator_11 (
    .first(first[10]), .second(second[10]), .previous(summator_10_remain), .remain(summator_11_remain),
    .current(sum12bit[10]));
  SUMMATOR summator_12 (
    .first(first[11]), .second(second[11]), .previous(summator_11_remain), .remain(remain),
    .current(sum12bit[11]));
endmodule

module BITS24SUMMATOR (
  input  [23:0] first,
  input  [23:0] second,
  output [23:0] sum24bit,
  output remain
);

  wire bits12summator_1_remain;

  BITS12SUMMATOR bits12summator_1 (
    .first(first[11:0]), .prevC(1'b0), .second(second[11:0]), .sum12bit(sum24bit[11:0]),
    .remain(bits12summator_1_remain));
  BITS12SUMMATOR bits12summator_2 (
    .first(first[23:12]), .prevC(bits12summator_1_remain), .second(second[23:12]),
    .sum12bit(sum24bit[23:12]), .remain(remain));
endmodule

module num12 (
  input  [11:0] inp,
  input  ReadWrite,
  input  Enable,
  output [11:0] num
);

  wire d_triggers_1_nq, d_triggers_2_nq, d_triggers_3_nq, d_triggers_4_nq, d_triggers_5_nq, d_triggers_6_nq,
       d_triggers_7_nq, d_triggers_8_nq, d_triggers_9_nq, d_triggers_10_nq, d_triggers_11_nq,
       d_triggers_12_nq;

  D_Triggers d_triggers_1 (.CLK(ReadWrite), .Data(inp[0]), .Enable(Enable), .Q(num[0]), .NQ(d_triggers_1_nq));
  // NoConnect on d_triggers_1_nq
  D_Triggers d_triggers_2 (.CLK(ReadWrite), .Data(inp[1]), .Enable(Enable), .Q(num[1]), .NQ(d_triggers_2_nq));
  // NoConnect on d_triggers_2_nq
  D_Triggers d_triggers_3 (.CLK(ReadWrite), .Data(inp[2]), .Enable(Enable), .Q(num[2]), .NQ(d_triggers_3_nq));
  // NoConnect on d_triggers_3_nq
  D_Triggers d_triggers_4 (.CLK(ReadWrite), .Data(inp[3]), .Enable(Enable), .Q(num[3]), .NQ(d_triggers_4_nq));
  // NoConnect on d_triggers_4_nq
  D_Triggers d_triggers_5 (.CLK(ReadWrite), .Data(inp[4]), .Enable(Enable), .Q(num[4]), .NQ(d_triggers_5_nq));
  // NoConnect on d_triggers_5_nq
  D_Triggers d_triggers_6 (.CLK(ReadWrite), .Data(inp[5]), .Enable(Enable), .Q(num[5]), .NQ(d_triggers_6_nq));
  // NoConnect on d_triggers_6_nq
  D_Triggers d_triggers_7 (.CLK(ReadWrite), .Data(inp[6]), .Enable(Enable), .Q(num[6]), .NQ(d_triggers_7_nq));
  // NoConnect on d_triggers_7_nq
  D_Triggers d_triggers_8 (.CLK(ReadWrite), .Data(inp[7]), .Enable(Enable), .Q(num[7]), .NQ(d_triggers_8_nq));
  // NoConnect on d_triggers_8_nq
  D_Triggers d_triggers_9 (.CLK(ReadWrite), .Data(inp[8]), .Enable(Enable), .Q(num[8]), .NQ(d_triggers_9_nq));
  // NoConnect on d_triggers_9_nq
  D_Triggers d_triggers_10 (.CLK(ReadWrite), .Data(inp[9]), .Enable(Enable), .Q(num[9]), .NQ(d_triggers_10_nq));
  // NoConnect on d_triggers_10_nq
  D_Triggers d_triggers_11 (.CLK(ReadWrite), .Data(inp[10]), .Enable(Enable), .Q(num[10]), .NQ(d_triggers_11_nq));
  // NoConnect on d_triggers_11_nq
  D_Triggers d_triggers_12 (.CLK(ReadWrite), .Data(inp[11]), .Enable(Enable), .Q(num[11]), .NQ(d_triggers_12_nq));
  // NoConnect on d_triggers_12_nq
endmodule

module num16 (
  input  [15:0] inp,
  input  ReadWrite,
  input  Enable,
  output [15:0] num
);

  wire d_triggers_1_nq, d_triggers_2_nq, d_triggers_3_nq, d_triggers_4_nq, d_triggers_5_nq, d_triggers_6_nq,
       d_triggers_7_nq, d_triggers_8_nq, d_triggers_9_nq, d_triggers_10_nq, d_triggers_11_nq,
       d_triggers_12_nq, d_triggers_13_nq, d_triggers_14_nq, d_triggers_15_nq, d_triggers_16_nq;

  D_Triggers d_triggers_1 (.CLK(ReadWrite), .Data(inp[0]), .Enable(Enable), .Q(num[0]), .NQ(d_triggers_1_nq));
  // NoConnect on d_triggers_1_nq
  D_Triggers d_triggers_2 (.CLK(ReadWrite), .Data(inp[1]), .Enable(Enable), .Q(num[1]), .NQ(d_triggers_2_nq));
  // NoConnect on d_triggers_2_nq
  D_Triggers d_triggers_3 (.CLK(ReadWrite), .Data(inp[2]), .Enable(Enable), .Q(num[2]), .NQ(d_triggers_3_nq));
  // NoConnect on d_triggers_3_nq
  D_Triggers d_triggers_4 (.CLK(ReadWrite), .Data(inp[3]), .Enable(Enable), .Q(num[3]), .NQ(d_triggers_4_nq));
  // NoConnect on d_triggers_4_nq
  D_Triggers d_triggers_5 (.CLK(ReadWrite), .Data(inp[4]), .Enable(Enable), .Q(num[4]), .NQ(d_triggers_5_nq));
  // NoConnect on d_triggers_5_nq
  D_Triggers d_triggers_6 (.CLK(ReadWrite), .Data(inp[5]), .Enable(Enable), .Q(num[5]), .NQ(d_triggers_6_nq));
  // NoConnect on d_triggers_6_nq
  D_Triggers d_triggers_7 (.CLK(ReadWrite), .Data(inp[6]), .Enable(Enable), .Q(num[6]), .NQ(d_triggers_7_nq));
  // NoConnect on d_triggers_7_nq
  D_Triggers d_triggers_8 (.CLK(ReadWrite), .Data(inp[7]), .Enable(Enable), .Q(num[7]), .NQ(d_triggers_8_nq));
  // NoConnect on d_triggers_8_nq
  D_Triggers d_triggers_9 (.CLK(ReadWrite), .Data(inp[8]), .Enable(Enable), .Q(num[8]), .NQ(d_triggers_9_nq));
  // NoConnect on d_triggers_9_nq
  D_Triggers d_triggers_10 (.CLK(ReadWrite), .Data(inp[9]), .Enable(Enable), .Q(num[9]), .NQ(d_triggers_10_nq));
  // NoConnect on d_triggers_10_nq
  D_Triggers d_triggers_11 (.CLK(ReadWrite), .Data(inp[10]), .Enable(Enable), .Q(num[10]), .NQ(d_triggers_11_nq));
  // NoConnect on d_triggers_11_nq
  D_Triggers d_triggers_12 (.CLK(ReadWrite), .Data(inp[11]), .Enable(Enable), .Q(num[11]), .NQ(d_triggers_12_nq));
  // NoConnect on d_triggers_12_nq
  D_Triggers d_triggers_13 (.CLK(ReadWrite), .Data(inp[12]), .Enable(Enable), .Q(num[12]), .NQ(d_triggers_13_nq));
  // NoConnect on d_triggers_13_nq
  D_Triggers d_triggers_14 (.CLK(ReadWrite), .Data(inp[13]), .Enable(Enable), .Q(num[13]), .NQ(d_triggers_14_nq));
  // NoConnect on d_triggers_14_nq
  D_Triggers d_triggers_15 (.CLK(ReadWrite), .Data(inp[14]), .Enable(Enable), .Q(num[14]), .NQ(d_triggers_15_nq));
  // NoConnect on d_triggers_15_nq
  D_Triggers d_triggers_16 (.CLK(ReadWrite), .Data(inp[15]), .Enable(Enable), .Q(num[15]), .NQ(d_triggers_16_nq));
  // NoConnect on d_triggers_16_nq
endmodule

module num24 (
  input  [23:0] inp,
  input  ReadWrite,
  input  Enable,
  output [23:0] num
);

  num12 num12_1 (.inp(inp[11:0]), .ReadWrite(ReadWrite), .Enable(Enable), .num(num[11:0]));
  num12 num12_2 (.inp(inp[23:12]), .ReadWrite(ReadWrite), .Enable(Enable), .num(num[23:12]));
endmodule

module zero (
  input  detnegzero,
  output [15:0] zero16
);


  assign zero16 = {detnegzero, {15{1'b0}}};
endmodule

module NaN (
  input  detnan,
  input  sign,
  input  [4:0] exp,
  input  [11:0] mantis,
  output [15:0] correctNaN_mbnothing
);

  wire not_1_out;
  wire [11:0] to12_1_bit12, to12_2_bit12;
  wire [11:9] and_3_out;
  wire [15:0] and_3_out_2, and_4_out, and_5_out, to16_1_bit16, to16_2_bit16;

  To12 to12_1 (.\bit (detnan), .bit12(to12_1_bit12));
  and and_1 (and_3_out_2[14], exp[0], exp[1], exp[3], exp[4], detnan);
  and and_2 (and_3_out_2[15], detnan, and_3_out_2[14], sign);
  assign {and_3_out, and_3_out_2[8:0]} = to12_1_bit12 & to12_2_bit12 & mantis;  // AND_Gate and_3, 12 bits wide
  To16 to16_1 (.\bit (detnan), .bit16(to16_1_bit16));
  not not_1 (not_1_out, and_3_out_2[14]);
  To12 to12_2 (.\bit (and_3_out_2[14]), .bit12(to12_2_bit12));
  assign and_4_out = 16'hfe00 & to16_1_bit16;  // AND_Gate and_4, 16 bits wide
  To16 to16_2 (.\bit (not_1_out), .bit16(to16_2_bit16));
  assign and_5_out = and_4_out & to16_2_bit16;  // AND_Gate and_5, 16 bits wide
  assign correctNaN_mbnothing = and_5_out | {and_3_out_2[15:14], {4{and_3_out_2[14]}}, detnan, and_3_out_2[8:0]};  // OR_Gate or_1, 16 bits wide
endmodule

module pinf (
  input  detpinf,
  output [15:0] outpt
);

  wire [15:0] to16_1_bit16;

  To16 to16_1 (.\bit (detpinf), .bit16(to16_1_bit16));
  assign outpt = 16'h7c00 & to16_1_bit16;  // AND_Gate and_1, 16 bits wide
endmodule

module detecting (
  input  sign,
  input  [11:0] mantis,
  input  [4:0] exp,
  output negzero,
  output PINF,
  output NAN
);

  wire and_1_out, and_3_out, and_4_out, not_1_out, not_2_out, not_3_out, or_1_out, or_2_out, or_3_out;

  or or_1 (or_1_out, mantis[0], mantis[1], mantis[2], mantis[3], mantis[4], mantis[5], mantis[6], mantis[7], mantis[8], mantis[9]);
  or or_2 (or_2_out, exp[0], exp[1], exp[2], exp[3], exp[4]);
  and and_1 (and_1_out, exp[0], exp[1], exp[2], exp[3], exp[4]);
  or or_3 (or_3_out, or_1_out, or_2_out);
  not not_1 (not_1_out, or_3_out);
  and and_2 (negzero, sign, not_1_out);
  not not_2 (not_2_out, sign);
  not not_3 (not_3_out, or_1_out);
  and and_3 (and_3_out, or_1_out, and_1_out);
  and and_4 (and_4_out, sign, or_3_out);
  and and_5 (PINF, not_2_out, not_3_out, and_1_out);
  or or_4 (NAN, and_3_out, and_4_out);
endmodule

module correcting (
  input  [11:0] mantis,
  input  [4:0] exp,
  output [4:0] realexp,
  output [11:0] man
);

  wire detectexp_1_is_even;
  wire [4:0] alignment_1_shiftexp, and_1_out, and_2_out, and_3_out, and_6_out, detectexp_1_correct_exp,
       fixexp_1_exp;
  wire [4:4] not_1_out, or_1_out, or_2_out;
  wire [11:0] alignment_1_man, and_4_out, and_5_out, and_7_out, and_8_out, normedmantis_1_normedman,
       normedmantis_1_shift, realmantis_1_realman, to12_1_bit12, to12_2_bit12, to12_3_bit12;

  or or_1 (or_1_out[4], exp[0], exp[1], exp[2], exp[3], exp[4]);
  detectexp detectexp_1 (.exp(exp), .correct_exp(detectexp_1_correct_exp), .is_even(detectexp_1_is_even));
  or or_2 (or_2_out[4], mantis[0], mantis[1], mantis[2], mantis[3], mantis[4], mantis[5], mantis[6], or_1_out[4], mantis[7], mantis[8], mantis[9], mantis[10], mantis[11]);
  fixexp fixexp_1 (.correctedexp(detectexp_1_correct_exp), .exp(fixexp_1_exp));
  not not_1 (not_1_out[4], or_1_out[4]);
  assign and_1_out = fixexp_1_exp;  // AND_Gate and_1, 5 bits wide AND_Gate
  To12 to12_1 (.\bit (or_2_out[4]), .bit12(to12_1_bit12));
  To12 to12_2 (.\bit (not_1_out[4]), .bit12(to12_2_bit12));
  To12 to12_3 (.\bit (or_1_out[4]), .bit12(to12_3_bit12));
  realmantis realmantis_1 (.detectexp(detectexp_1_is_even), .mantis(mantis), .realman(realmantis_1_realman));
  normedmantis normedmantis_1 (.mantis(mantis), .normedman(normedmantis_1_normedman), .shift(normedmantis_1_shift));
  assign and_2_out = {5{or_2_out[4]}} & and_1_out;  // AND_Gate and_2, 5 bits wide
  alignment alignment_1 (
    .normedmantis(normedmantis_1_normedman), .shift(normedmantis_1_shift), .man(alignment_1_man),
    .shiftexp(alignment_1_shiftexp));
  assign and_3_out = {5{not_1_out[4]}} & alignment_1_shiftexp;  // AND_Gate and_3, 5 bits wide
  assign and_4_out = to12_2_bit12 & alignment_1_man;  // AND_Gate and_4, 12 bits wide
  assign and_5_out = to12_3_bit12 & realmantis_1_realman;  // AND_Gate and_5, 12 bits wide
  assign and_6_out = and_3_out & {5{or_2_out[4]}};  // AND_Gate and_6, 5 bits wide
  assign and_7_out = and_4_out & to12_1_bit12;  // AND_Gate and_7, 12 bits wide
  assign and_8_out = to12_1_bit12 & and_5_out;  // AND_Gate and_8, 12 bits wide
  assign realexp = and_6_out | and_2_out;  // OR_Gate or_3, 5 bits wide
  assign man = and_7_out | and_8_out;  // OR_Gate or_4, 12 bits wide
endmodule

module realmantis (
  input  detectexp,
  input  [11:0] mantis,
  output [11:0] realman
);

  wire [11:0] and_1_out, and_2_out, l12_1_outp, not_1_out, to12_1_bit12;

  To12 to12_1 (.\bit (detectexp), .bit12(to12_1_bit12));
  L12 l12_1 (.inp({2'b01, mantis[9:0]}), .outp(l12_1_outp));
  assign not_1_out = ~to12_1_bit12;  // NOT_Gate not_1, 12 bits wide
  assign and_1_out = not_1_out & {2'b01, mantis[9:0]};  // AND_Gate and_1, 12 bits wide
  assign and_2_out = to12_1_bit12 & l12_1_outp;  // AND_Gate and_2, 12 bits wide
  assign realman = and_2_out | and_1_out;  // OR_Gate or_1, 12 bits wide
endmodule

module beg (
  input  CLK,
  input  ENABLE,
  output NQ,
  output equal,
  output greater
);

  wire d_triggers_1_nq, d_triggers_1_q, not_1_out;
  wire [23:0] bits24summator_1_sum24bit, num24_1_num, num24_2_num;

  not not_1 (not_1_out, CLK);
  num24 num24_1 (.inp(bits24summator_1_sum24bit), .ReadWrite(CLK), .Enable(ENABLE), .num(num24_1_num));
  D_Triggers d_triggers_1 (
    .CLK(d_triggers_1_nq), .Data(CLK), .Enable(ENABLE), .Q(d_triggers_1_q), .NQ(d_triggers_1_nq));
  CompC compc_1 (.first(num24_1_num), .second(24'h1), .equal(equal), .greater(greater));  // open: less
  num24 num24_2 (.inp(num24_1_num), .ReadWrite(not_1_out), .Enable(ENABLE), .num(num24_2_num));
  D_Triggers d_triggers_2 (.CLK(not_1_out), .Data(d_triggers_1_q), .Enable(ENABLE), .NQ(NQ));  // open: Q
  BITS24SUMMATOR bits24summator_1 (
    .first(num24_2_num), .second(24'h1), .sum24bit(bits24summator_1_sum24bit));  // open: remain
endmodule

module alignment (
  input  [11:0] normedmantis,
  input  [11:0] shift,
  output [11:0] man,
  output [4:0] shiftexp
);

  wire [11:0] bits12summator_1_sum12bit, l12_1_outp, not_1_out, or_1_out, or_2_out, or_3_out, r12_1_outp,
       to12_1_bit12;
  wire [11:5] bits12difc_1_dif12bit;

  L12 l12_1 (.inp(normedmantis), .outp(l12_1_outp));
  To12 to12_1 (.\bit (shift[0]), .bit12(to12_1_bit12));
  BITS12SUMMATOR bits12summator_1 (
    .first(shift), .second(12'h1), .sum12bit(bits12summator_1_sum12bit));  // open: prevC, remain
  assign not_1_out = ~to12_1_bit12;  // NOT_Gate not_1, 12 bits wide
  R12 r12_1 (.inp(bits12summator_1_sum12bit), .outp(r12_1_outp));
  assign or_1_out = normedmantis | l12_1_outp;  // OR_Gate or_1, 12 bits wide
  assign or_2_out = normedmantis | to12_1_bit12;  // OR_Gate or_2, 12 bits wide
  assign or_3_out = l12_1_outp | not_1_out;  // OR_Gate or_3, 12 bits wide
  BITS12DifC bits12difc_1 (
    .first(12'h8), .second(r12_1_outp), .dif12bit({bits12difc_1_dif12bit, shiftexp}));  // open: prevC, remain
  assign man = or_1_out & or_2_out & or_3_out;  // AND_Gate and_1, 12 bits wide
endmodule

module fixexp (
  input  [4:0] correctedexp,
  output [4:0] exp
);

  wire bits12summator_1_remain;
  wire [11:0] bits12summator_1_sum12bit;
  wire [11:5] r12_1_outp;

  BITS12SUMMATOR bits12summator_1 (
    .first(12'hf), .second({{7{1'b0}}, correctedexp}), .sum12bit(bits12summator_1_sum12bit),
    .remain(bits12summator_1_remain));  // open: prevC
  // NoConnect on bits12summator_1_remain
  R12 r12_1 (.inp(bits12summator_1_sum12bit), .outp({r12_1_outp, exp}));
endmodule
